# Fritzing sketch fishlamp.timer (saved by Fritzing 0.6.3b)
breadboards: 1

parts:
  IC1 = IC, DIP package, 16 pins [chip_label=MAX232 spacing=300mil]
  Power_plug1 = Power plug
  U1 = Voltage Regulator - 5V [package="TO220 [THT]"]
  C1 = Electrolytic Capacitor [capacitance=10µF package="100 mil [THT, electrolytic]"]
  C2 = Electrolytic Capacitor [capacitance=1µF package="100 mil [THT, electrolytic]"]
  C3 = Electrolytic Capacitor [capacitance=1µF package="100 mil [THT, electrolytic]"]
  C4 = Electrolytic Capacitor [capacitance=1µF package="100 mil [THT, electrolytic]"]
  C5 = Electrolytic Capacitor [capacitance=1µF package="100 mil [THT, electrolytic]"]
  C6 = Electrolytic Capacitor [capacitance=1µF package="100 mil [THT, electrolytic]"]
  CN1 = DB9_rt_female
  J1 = female pin header, 1 pin [form="♂ (male)"]
  J2 = female pin header, 1 pin [form="♂ (male)"]
  C7 = Electrolytic Capacitor [capacitance=1µF package="100 mil [THT, electrolytic]"]
  J3 = female pin header, 6 pins [form="♂ (male)"]
  IC2 = IC, DIP package, 20 pins [chip_label=PIC18F14K50 spacing=300mil]
  Relay = IC, DIP package, 10 pins [chip_label=Relay spacing=300mil]
  R1 = Resistor [tolerance=±5% resistance=220 package=THT]
  R2 = Resistor [tolerance=±5% resistance=220 package=THT]
  C8 = Electrolytic Capacitor [capacitance=1µF package="100 mil [THT, electrolytic]"]
  Q1 = NPN-Transistor [package="TO92 [THT]"]
  Q2 = NPN-Transistor [package="TO92 [THT]"]
  J4 = Screw terminal - 2 pins [package=THT]

nets:
  N1: IC1.pin1, C3.+
  N2: IC1.pin2, C5.+
  N3: IC1.pin3, C3.-
  N4: IC1.pin4, C4.+
  N5: IC1.pin5, C4.-
  N6: IC1.pin6, C6.+
  N7: IC1.pin11, IC2.pin10
  N8: IC1.pin12, IC2.pin12
  N9: IC1.pin13, CN1.connector2
  N10: IC1.pin14, CN1.connector1
  GND: IC1.pin15, Power_plug1.GND, U1.GND, C1.-, C2.-, C5.-, C6.-, CN1.connector4, C7.-, J3.pin3, IC2.pin20, R1.Pin_1, R2.Pin_1, C8.+
  N11: IC1.pin16, U1.output_voltage, C2.+, C7.+, J3.pin2, IC2.pin1, Relay.pin1, Relay.pin10, C8.-
  N12: Power_plug1.VCC, U1.input_voltage, C1.+
  N13: CN1.connector0, CN1.connector3, CN1.connector5, J1.pin1
  N14: CN1.connector6, CN1.connector7, J2.pin1
  N15: J3.pin1, IC2.pin4
  N16: J3.pin4, IC2.pin19
  N17: J3.pin5, IC2.pin18
  N18: J3.pin6, IC2.pin3
  N19: IC2.pin5, Q1.B
  N20: IC2.pin6, Q2.B
  N21: Relay.pin5, Q1.C
  N22: Relay.pin6, Q2.C
  N23: Relay.pin7, J4.pin2
  N24: Relay.pin8, J4.pin1
  N25: R1.Pin_0, Q1.E
  N26: R2.Pin_0, Q2.E

notes:
  FishLamp.v1
